# Fritzing sketch DRO (saved by Fritzing 0.9.10b)
circuit board: 7.3cm x 7cm
breadboards: 1

parts:
  Onderdeel1 = Arduino Nano (Rev3.0)
  R1 = Resistor [tolerance=±5% power=0.25 resistance=10k package=THT]
  J3 = female pin header, 2 pins [form="♀ (female)"]
  R2 = Resistor [tolerance=±5% power=0.25 resistance=20k package=THT]
  J4 = female pin header, 2 pins [form="♀ (female)"]
  J5 = female pin header, 2 pins [form="♀ (female)"]
  C1 = Ceramic Capacitor [capacitance=100nF voltage=35V package="100 mil [THT, multilayer]"]
  J2 = rounded female pin header, 4 pins [form="♀ (female rounded)"]
  J1 = female pin header, 4 pins [form="♀ (female)"]

nets (from the schematic view):
  N1: Onderdeel1.GND, J3.pin2, R2.Pin_0, J5.pin2, C1.0, J2.pin1, J1.pin2
  N2: Onderdeel1.D2, R1.Pin_0
  N3: Onderdeel1.D3, J2.pin3
  N4: Onderdeel1.D9, J5.pin1, C1.1
  N5: Onderdeel1.VIN, J4.pin2
  N6: Onderdeel1.5V, J1.pin1
  N7: Onderdeel1.A5, J1.pin3
  N8: Onderdeel1.A4, J1.pin4
  N9: Onderdeel1.3V3, J2.pin4
  N10: R1.Pin_1, R2.Pin_1, J2.pin2
  N11: J3.pin1, J4.pin1

notes:
  batt.
  switch
  sensor
  reset
  oled
  arduino
  -
  +
  Wout Berggren
  jan 2023
  V 1.0
  DRO oled display
